# Fritzing sketch CircuitoMixto (saved by Fritzing 0.9.1b)
breadboards: 1

parts:
  R1 = Resistor [tolerance=±5% resistance=1k package=THT]
  V1 = DC Power [voltage=5]
  R2 = Resistor [tolerance=±5% resistance=220 package=THT]
  R3 = Resistor [tolerance=±5% resistance=220 package=THT]
  R4 = Resistor [tolerance=±5% resistance=10k package=THT]

nets:
  N1: R1.Pin_0, V1.V+
  N2: R1.Pin_1, R2.Pin_0, R3.Pin_0
  GND: V1.V-, R2.Pin_1, R4.Pin_1
  N3: R3.Pin_1, R4.Pin_0
