# Fritzing sketch CircuitoParalelo (saved by Fritzing 0.9.1b)
breadboards: 1

parts:
  R1 = Resistor [tolerance=±5% resistance=220 package=THT]
  R2 = Resistor [tolerance=±5% resistance=1k package=THT]
  R3 = Resistor [tolerance=±5% resistance=220 package=THT]
  V1 = DC Power [voltage=5]

nets:
  N1: R1.Pin_0, R2.Pin_0, R3.Pin_0, V1.V+
  GND: R1.Pin_1, R2.Pin_1, R3.Pin_1, V1.V-
