# Fritzing sketch LedPushButton (saved by Fritzing 0.9.1b)
breadboards: 1

parts:
  Part1 = Arduino Uno (Rev3)
  R1 = Resistor [tolerance=±5% resistance=220 package="0603 [SMD]"]
  LED1 = smd LED [color="Red (633nm)" package="0603 [SMD]"]
  S1 = Pushbutton [package="[THT]"]
  R2 = Resistor [tolerance=±5% resistance=10k package=THT]

nets:
  N1: Part1.D13/SCK, S1.Pin_3, S1.Pin_4, R2.Pin_1
  N2: Part1.D2, R1.Pin_0
  5V: Part1.5V, R2.Pin_0
  GND: Part1.GND, LED1.cathode, S1.Pin_1, S1.Pin_2
  N3: R1.Pin_1, LED1.anode

// code stored in the sketch: LedPushButton.ino
const int LED = 2;
const int PB = 13;

int buttonState;

void setup() {
    pinMode(LED, OUTPUT);
    pinMode(PB, INPUT);
}

void loop() {
  // put your main code here, to run repeatedly:
  buttonState = digitalRead(PB);
  if (buttonState == HIGH) {     
    // turn LED on:    
    digitalWrite(LED, HIGH);  
  } 
  else {
    // turn LED off:
    digitalWrite(LED, LOW); 
  }
  delay(10);
}
