# Fritzing sketch photoresistor (saved by Fritzing 0.9.1b)
breadboards: 1

parts:
  U1 = TLP621 [package=THT]
  Part1 = Arduino Uno (Rev3)
  R1 = Resistor [tolerance=±5% resistance=220 package=THT]
  U2 = RELAY-2 [package=relay-g5v]
  D1 = Rectifier Diode [package="Melf DO-213 AA [SMD]"]
  J1 = Power Jack [package=power_jack_slot]
  R2 = PHOTOCELL [package=photocell-kit]
  R3 = Trimmer Potentiometer [maximum_resistance=10kΩ package=THT]
  R4 = Resistor [tolerance=±5% resistance=1k package=THT]
  Q1 = TRANSISTOR_NPN [package=to-92]

nets (from the schematic view):
  N1: U1.Pin_1, R1.Pin_1
  N2: U1.Pin_2, Part1.D13/SCK
  N3: U1.Pin_4, U2.9, D1.cathode, J1.GNDBREAK
  N4: U1.Pin_3, R4.Pin_0
  N5: Part1.A0, R2.P$2, R3.leg1
  N6: Part1.GND, R3.leg2
  N7: Part1.5V, R1.Pin_0, R2.P$1
  N8: U2.2, D1.anode, Q1.C
  N9: J1.GND, Q1.E
  N10: R4.Pin_1, Q1.B

// code stored in the sketch: LedPushButton.ino
const int LED = 2;
const int PB = 13;

int buttonState;

void setup() {
    pinMode(LED, OUTPUT);
    pinMode(PB, INPUT);
}

void loop() {
  // put your main code here, to run repeatedly:
  buttonState = digitalRead(PB);
  if (buttonState == HIGH) {     
    // turn LED on:    
    digitalWrite(LED, HIGH);  
  } 
  else {
    // turn LED off:
    digitalWrite(LED, LOW); 
  }
  delay(10);
}

// code stored in the sketch: photoresistor.ino
const int photoResistor = A0;
const int relayOutput = 13;

int photoResistorValue;

void setup() {
    pinMode(relayOutput, OUTPUT);
}

void loop() {
  // put your main code here, to run repeatedly:
  photoResistorValue = analogRead(photoResistor);
  Serial.print(photoResistorValue);
  if (photoResistorValue > 500) {
    digitalWrite(relayOutput, HIGH);
  } 
  else {
    digitalWrite(relayOutput, LOW);
  }
  delay(10);
}
