# Fritzing sketch simulacion (saved by Fritzing 0.9.1b)
breadboards: 1

parts:
  Part1 = Arduino Uno (Rev3)
  R1 = Resistor [tolerance=±5% resistance=220 package=THT]
  LED1 = LED - 5mm [color="Red (633nm)" package="5 mm [THT]"]

nets (from the schematic view):
  N1: Part1.D9_PWM, R1.Pin_0
  GND: Part1.GND, LED1.cathode
  5V: Part1.VIN
  N2: R1.Pin_1, LED1.anode

// code stored in the sketch: codigo.ino
const int LED = 9;
int i = 0;

void setup() {
  pinMode(LED, OUTPUT);
}

void loop() {
	for (i = 0; i < 255; i++) { // loop from 0 to 254 (fade in)
		analogWrite(LED, i);
		// set the LED brightness
		delay(10); // Wait 10ms because analogWrite
		// is instantaneous and we would
		// not see any change
	}
	
	for (i = 255; i > 0; i--) { // loop from 255 to 1 (fade out)
		analogWrite(LED, i); // set the LED brightness
		delay(10);
	// Wait 10ms
	}
}
